// Logisim project AMBA-APB.circ as structural Verilog: 3 circuits, main circuit FSM Controller
module FSM_Controller (
  input  in_1,
  input  [7:0] datain,
  input  [1:0] addr,
  input  R_W,
  input  TRANSACTION,
  output PENABLE,
  output [7:0] out_7,
  output [1:0] out_8,
  output out_9,
  output PSEL
);

  wire and_1_out, and_2_out, d_ff_2_q, not_1_out, not_2_out;

  not not_1 (not_1_out, d_ff_2_q);
  and and_1 (and_1_out, not_1_out, TRANSACTION);
  D_Flip_Flop d_ff_1 (.clk(in_1), .D(d_ff_2_q), .Q(PENABLE));  // open: Qn, preset, en, reset
  D_Flip_Flop d_ff_2 (.clk(in_1), .D(and_1_out), .Q(d_ff_2_q));  // open: Qn, preset, en, reset
  or or_1 (PSEL, PENABLE, d_ff_2_q);
  not not_2 (not_2_out, d_ff_2_q);
  Register register_1 (.D(datain), .en(and_2_out), .Q(out_7), .clk(in_1));  // open: clr
  and and_2 (and_2_out, not_2_out, TRANSACTION);
  Register #(.width(2)) register_2 (.D(addr), .en(and_2_out), .Q(out_8), .clk(in_1));  // open: clr
  Register #(.width(1)) register_3 (.D(R_W), .en(and_2_out), .Q(out_9), .clk(in_1));  // open: clr
endmodule

module Slave_Mem (
  input  [7:0] datain,
  input  [1:0] addr,
  input  R_W,
  input  Enable,
  input  Sel,
  input  ready_M,
  input  clk,
  input  clr,
  input  parity,
  output [7:0] dataOut,
  output valid_S
);

  wire and_1_out, and_2_out, decoder_1_out0, decoder_1_out1, decoder_1_out2, decoder_1_out3, not_1_out,
       or_1_out;
  wire [7:0] register_1_q, register_2_q, register_3_q, register_4_q;

  or or_1 (or_1_out, Sel, Enable);
  Decoder #(.select(2), .disabled(0)) decoder_1 (
    .out0(decoder_1_out0), .out1(decoder_1_out1), .out2(decoder_1_out2), .out3(decoder_1_out3), .sel(addr),
    .en(and_1_out));
  and and_1 (and_1_out, R_W, or_1_out);
  Register register_1 (.D(datain), .en(decoder_1_out0), .Q(register_1_q), .clk(clk), .clr(clr));
  Register register_2 (.D(datain), .en(decoder_1_out1), .Q(register_2_q), .clk(clk), .clr(clr));
  Register register_3 (.D(datain), .en(decoder_1_out2), .Q(register_3_q), .clk(clk), .clr(clr));
  Register register_4 (.D(datain), .en(decoder_1_out3), .Q(register_4_q), .clk(clk), .clr(clr));
  Multiplexer #(.select(2), .width(8)) multiplexer_1 (
    .in0(register_1_q), .in1(register_2_q), .in2(register_3_q), .in3(register_4_q), .out(dataOut),
    .sel(addr), .en(and_2_out));
  and and_2 (and_2_out, not_1_out, ready_M);
  not not_1 (not_1_out, R_W);

  assign valid_S = parity;

  // Notes on the sheet:
  //   0 = read
  //   1 = write
endmodule

module Main_Bridge (
  input  [7:0] datain,
  input  [1:0] addr,
  input  R_W,
  input  clr,
  input  in_5,
  output [7:0] dataOut
);

  wire clock_1_out, fsm_controller_1_out_9, fsm_controller_1_penable, fsm_controller_1_psel;
  wire [1:0] fsm_controller_1_out_8;
  wire [7:0] fsm_controller_1_out_7;

  Clock clock_1 (.out(clock_1_out));
  FSM_Controller fsm_controller_1 (
    .in_1(clock_1_out), .PENABLE(fsm_controller_1_penable), .TRANSACTION(in_5), .PSEL(fsm_controller_1_psel),
    .datain(datain), .addr(addr), .R_W(R_W), .out_7(fsm_controller_1_out_7), .out_8(fsm_controller_1_out_8),
    .out_9(fsm_controller_1_out_9));
  Slave_Mem slave_mem_1 (
    .datain(fsm_controller_1_out_7), .addr(fsm_controller_1_out_8), .R_W(fsm_controller_1_out_9),
    .Enable(fsm_controller_1_penable), .Sel(fsm_controller_1_psel), .ready_M(1'b1), .clk(clock_1_out),
    .clr(clr), .dataOut(dataOut));  // open: parity, valid_S
endmodule
