// Logisim project HANDSHAKE PROTOCOL.circ as structural Verilog: 1 circuit, main circuit main
module main (
  input  [7:0] DATA_IN,
  input  W_R,
  input  VALID_M,
  input  READY_S,
  input  [1:0] ADDRESS,
  input  VALID_S,
  input  READY_M,
  output [7:0] DATA_OUT
);

  wire and_1_out, and_2_out, clock_1_out, decoder_1_out0, decoder_1_out1, decoder_1_out2, decoder_1_out3,
       not_1_out;
  wire [7:0] a_q, b_q, control_q, result_q;

  Clock clock_1 (.out(clock_1_out));
  and and_1 (and_1_out, W_R, VALID_M, READY_S);
  Decoder #(.select(2)) decoder_1 (
    .out0(decoder_1_out0), .out1(decoder_1_out1), .out2(decoder_1_out2), .out3(decoder_1_out3),
    .sel(ADDRESS), .en(and_1_out));
  Register a (.D(DATA_IN), .en(decoder_1_out0), .Q(a_q), .clk(clock_1_out));  // open: clr
  Register b (.D(DATA_IN), .en(decoder_1_out1), .Q(b_q), .clk(clock_1_out));  // open: clr
  Register control (.D(DATA_IN), .en(decoder_1_out2), .Q(control_q), .clk(clock_1_out));  // open: clr
  Register result (.D(DATA_IN), .en(decoder_1_out3), .Q(result_q), .clk(clock_1_out));  // open: clr
  not not_1 (not_1_out, W_R);
  and and_2 (and_2_out, not_1_out, VALID_S, READY_M);
  Multiplexer #(.select(2), .width(8)) multiplexer_1 (
    .in0(a_q), .in1(b_q), .in2(control_q), .in3(result_q), .out(DATA_OUT), .sel(ADDRESS), .en(and_2_out));

  // Notes on the sheet:
  //   HAND SHAKE PROTOCOL
endmodule
